// Logisim project add2.circ as structural Verilog: 1 circuit, main circuit main
module main (
  input  in_1,
  input  [3:0] in_2,
  input  [3:0] in_3,
  output [3:0] out_4,
  output out_5
);

  wire undriven, undriven_2, undriven_3;

  Adder #(.width(1)) adder_1 (.a(undriven), .cin(in_1));  // open: b, out, cout
  Adder #(.width(1)) adder_2 (.b(undriven_2));  // open: a, out, cin, cout
  Adder #(.width(1)) adder_3 ();  // open: a, b, out, cin, cout
  Adder #(.width(1)) adder_4 (.b(undriven_3));  // open: a, out, cin, cout
endmodule
