// Logisim project latch_flipflop_register.circ as structural Verilog: 3 circuits, main circuit main
module main (
  input  CLK,
  input  [3:0] X,
  output [3:0] Y
);

  flipflop flipflop_1 (.D(X[3]), .CLK(CLK), .Q(Y[2]));  // open: Qout
  flipflop flipflop_2 (.D(X[3]), .CLK(CLK), .Q(Y[1]));  // open: Qout
  flipflop flipflop_3 (.D(X[3]), .CLK(CLK), .Q(Y[0]));  // open: Qout
  flipflop flipflop_4 (.D(X[3]), .CLK(CLK), .Q(Y[3]));  // open: Qout

  assign X[2:0] = {3{X[3]}};

  // Notes on the sheet:
  //   Q3
  //   Q2
  //   Q1
  //   Q0
endmodule

module Latch (
  input  CLK,
  input  D,
  output Q,
  output Qout
);

  wire and_1_out, and_2_out, not_1_out;

  not not_1 (not_1_out, D);
  and and_1 (and_1_out, CLK, not_1_out);
  and and_2 (and_2_out, CLK, D);
  nor nor_1 (Q, and_1_out, Qout);
  nor nor_2 (Qout, Q, and_2_out);
endmodule

module flipflop (
  input  D,
  input  CLK,
  output Q,
  output Qout
);

  wire latch_1_q, not_1_out;

  not not_1 (not_1_out, CLK);
  Latch latch_1 (.CLK(not_1_out), .D(D), .Q(latch_1_q));  // open: Qout
  Latch latch_2 (.CLK(CLK), .D(latch_1_q), .Q(Q), .Qout(Qout));

  // Notes on the sheet:
  //   leader
  //   follower
endmodule
