// Logisim project multiplex.circ as structural Verilog: 1 circuit, main circuit main
module main (
  input  in_1,
  input  in_2,
  input  in_3,
  input  [1:0] in_4,
  input  in_5,
  input  in_6,
  output out_7,
  output out_8
);

  wire multiplexer_1_out, multiplexer_2_out, multiplexer_4_out;

  Multiplexer multiplexer_1 (.in0(in_1), .in1(in_3), .out(multiplexer_1_out), .sel(in_4[0]));
  Multiplexer multiplexer_2 (.in0(in_5), .in1(in_6), .out(multiplexer_2_out), .sel(in_4[0]));
  Multiplexer #(.enable("true"), .select(2)) multiplexer_3 (
    .in0(in_1), .in1(in_3), .in2(in_5), .in3(in_6), .out(out_7), .sel(in_4), .en(in_2));
  Multiplexer multiplexer_4 (.in0(multiplexer_1_out), .in1(multiplexer_2_out), .out(multiplexer_4_out), .sel(in_4[1]));
  xor xor_1 (out_8, out_7, multiplexer_4_out);
endmodule
