// Logisim project noSubReg.circ as structural Verilog: 1 circuit, main circuit main
module main (
  input  [3:0] in_1,
  output [3:0] out_2
);

  wire and_1_out, and_2_out, and_3_out, and_4_out, and_5_out, and_6_out, and_7_out, and_8_out, clock_1_out,
       nor_2_out, nor_4_out, nor_6_out, nor_8_out, not_1_out, not_2_out, not_3_out, not_4_out;

  Clock clock_1 (.out(clock_1_out));
  not not_1 (not_1_out, in_1[2]);
  not not_2 (not_2_out, in_1[0]);
  not not_3 (not_3_out, in_1[1]);
  not not_4 (not_4_out, in_1[3]);
  and and_1 (and_1_out, clock_1_out, not_2_out);
  and and_2 (and_2_out, clock_1_out, in_1[0]);
  and and_3 (and_3_out, clock_1_out, not_3_out);
  and and_4 (and_4_out, clock_1_out, in_1[1]);
  and and_5 (and_5_out, clock_1_out, not_4_out);
  and and_6 (and_6_out, clock_1_out, in_1[3]);
  and and_7 (and_7_out, clock_1_out, not_1_out);
  and and_8 (and_8_out, clock_1_out, in_1[2]);
  nor nor_1 (out_2[3], and_1_out, nor_2_out);
  nor nor_2 (nor_2_out, out_2[3], and_2_out);
  nor nor_3 (out_2[2], and_3_out, nor_4_out);
  nor nor_4 (nor_4_out, out_2[2], and_4_out);
  nor nor_5 (out_2[1], and_5_out, nor_6_out);
  nor nor_6 (nor_6_out, out_2[1], and_6_out);
  nor nor_7 (out_2[0], and_7_out, nor_8_out);
  nor nor_8 (nor_8_out, out_2[0], and_8_out);

  // Notes on the sheet:
  //   X
  //   Y
endmodule
